# Fritzing sketch scheme (saved by Fritzing 0.9.2b)

parts:
  U1 = ESP8266 WiFi Module [part_number=ESP8266]
  3_3V = Voltage Regulator - 5V [package="TO220 [THT]"]
  U3 = 2-Channel 5v Relay Shield [package=relay-2ch5v10a]
  V1 = DC Power [voltage=12V]  # not connected
  5v = Power plug
  12v = Power plug
  12v_motor = DC Motor  # not connected
  Cancel_spikes_and_ripple_noises = Electrolytic Capacitor [capacitance=470µF package="100 mil [THT, electrolytic]"]  # not connected
  R1 = Resistor [tolerance=±5% resistance=300 package="1206 [SMD]"]  # not connected
  Transient_response_prevent_flash_mode = Electrolytic Capacitor [capacitance=10µF package="100 mil [THT, electrolytic]"]  # not connected
  U5 = TRANSISTOR_NPN_2 [package=to-92]
  2N2222 = TRANSISTOR_NPN_2 [package=to-92]
  R2 = Resistor [tolerance=±5% resistance=300 package="1206 [SMD]"]  # not connected
  R3 = Resistor [tolerance=±5% resistance=300 package="1206 [SMD]"]
  Decoupling_capacitor_improve_stability = Electrolytic Capacitor [capacitance=0.1µF package="100 mil [THT, electrolytic]"]  # not connected
  part = Electrolytic Capacitor [capacitance=10µF package="100 mil [THT, electrolytic]"]  # not connected
  Filter_47nF = Ceramic Capacitor [capacitance=4.7µF voltage=16V package="200 mil [THT, multilayer]"]

nets:
  N1: U1.GPIO_2, R3.Pin_1
  N2: U1.CH_PD, 3_3V.output_voltage
  N3: 3_3V.input_voltage, 5v.VCC
  GND: 3_3V.GND, 5v.GND
  N4: U3.IN1, 2N2222.E
  N5: U3.IN2, U5.E
  N6: U3.K1-In, Filter_47nF.1
  N7: U3.K1-Off, U3.K2-Off, 12v.GND
  N8: U3.K1-On, U3.K2-On, 12v.VCC
  N9: U3.K2-In, Filter_47nF.0

custom parts:
  ESP8266 WiFi Module: Generic WiFi Module based on the ESP8266 with onboard PCB antenna and UART communications
  2-Channel 5v Relay Shield: 2 Channel 5v Relay Shield w. 2x SPD-06VDC-SD-C
